// Logisim project gates.circ as structural Verilog: 1 circuit, main circuit main
module main (
  input  in_1,
  input  in_2,
  input  in_3,
  input  in_4,
  input  in_5,
  input  in_6,
  input  in_7,
  input  in_8,
  input  in_9,
  input  in_10,
  input  in_11
);

  wire and_1_out, and_2_out, and_3_out, and_4_out, not_1_out, not_2_out, not_3_out, not_4_out, not_5_out,
       or_1_out, or_2_out, or_3_out;

  not not_1 (not_1_out, in_9);
  not not_2 (not_2_out, in_8);
  or or_1 (or_1_out, in_1, in_2);
  not not_3 (not_3_out, in_3);
  and and_1 (and_1_out, in_10, in_11);
  LED led_1 (.in(not_3_out));
  LED led_2 (.in(and_2_out));
  and and_2 (and_2_out, in_4, in_5);
  LED led_3 (.in(or_2_out));
  or or_2 (or_2_out, in_6, in_7);
  and and_3 (and_3_out, in_8, not_1_out);
  and and_4 (and_4_out, in_9, not_2_out);
  not not_4 (not_4_out, and_1_out);
  not not_5 (not_5_out, or_1_out);
  LED led_4 (.in(not_5_out));
  LED led_5 (.in(not_4_out));
  or or_3 (or_3_out, and_3_out, and_4_out, and_4_out);
  LED led_6 (.in(or_3_out));

  // Notes on the sheet:
  //   XOR GATE
  //   NOT GATE
  //   AND GATE
  //   OR GATE
  //   XOR GATE
  //   NAND GATE
endmodule
